// Logisim project ALU.circ as structural Verilog
module LeftShift32 (
  input  Cn,
  input  [31:0] B,
  input  [4:0] Sa,
  output [31:0] C
);

  wire [31:0] multiplexer_1_out, multiplexer_2_out, multiplexer_3_out;
  wire [31:16] multiplexer_4_out, multiplexer_4_out_2;

  Multiplexer #(.width(32), .enable("false")) multiplexer_1 (
    .in0(B), .in1({B[30:0], Cn}), .out(multiplexer_1_out), .sel(Sa[0]));
  Multiplexer #(.width(32), .enable("false")) multiplexer_2 (
    .in0(multiplexer_1_out), .in1({multiplexer_1_out[29:0], {2{Cn}}}), .out(multiplexer_2_out), .sel(Sa[1]));
  Multiplexer #(.width(32), .enable("false")) multiplexer_3 (
    .in0(multiplexer_2_out), .in1({multiplexer_2_out[27:0], {4{Cn}}}), .out(multiplexer_3_out), .sel(Sa[2]));
  Multiplexer #(.width(32), .enable("false")) multiplexer_4 (
    .in0(multiplexer_3_out), .in1({multiplexer_3_out[23:0], {8{Cn}}}),
    .out({multiplexer_4_out_2, multiplexer_4_out}), .sel(Sa[3]));
  Multiplexer #(.width(32), .enable("false")) multiplexer_5 (
    .in0({multiplexer_4_out_2, multiplexer_4_out}), .in1({multiplexer_4_out, {16{Cn}}}), .out(C), .sel(Sa[4]));
endmodule

module LRShift32 (
  input  Op,
  input  [31:0] B,
  input  [4:0] Sa,
  input  Cin,
  output [31:0] C
);

  wire [31:0] flip32_1_flipa, flip32_2_flipa, leftshift32_1_c, multiplexer_1_out;

  Flip32 flip32_1 (.A(B), .FlipA(flip32_1_flipa));
  Multiplexer #(.width(32), .enable("false")) multiplexer_1 (
    .in0(B), .in1(flip32_1_flipa), .out(multiplexer_1_out), .sel(Op));
  LeftShift32 leftshift32_1 (.Cn(Cin), .B(multiplexer_1_out), .Sa(Sa), .C(leftshift32_1_c));
  Flip32 flip32_2 (.A(leftshift32_1_c), .FlipA(flip32_2_flipa));
  Multiplexer #(.width(32), .enable("false")) multiplexer_2 (
    .in0(leftshift32_1_c), .in1(flip32_2_flipa), .out(C), .sel(Op));
endmodule

module Flip32 (
  input  [31:0] A,
  output [31:0] FlipA
);


  assign FlipA = {A[0], A[1], A[2], A[3], A[4], A[5], A[6], A[7], A[8], A[9], A[10], A[11], A[12], A[13], A[14], A[15], A[16], A[17], A[18], A[19], A[20], A[21], A[22], A[23], A[24], A[25], A[26], A[27], A[28], A[29], A[30], A[31]};
endmodule
