// Logisim project Processor.circ as structural Verilog
// rising
module Register_File (
  input  [31:0] D,
  input  W,
  input  [4:0] Rw,
  input  [4:0] Ra,
  input  [3:0] Rb,
  output [31:0] Qa,
  output [31:0] Qb
);

  wire and_1_out, and_2_out, and_3_out, and_4_out, and_5_out, and_6_out, and_7_out, and_8_out, and_9_out,
       and_10_out, and_11_out, and_12_out, and_13_out, and_14_out, and_15_out, and_16_out, and_17_out,
       and_18_out, and_19_out, and_20_out, and_21_out, and_22_out, and_23_out, and_24_out, and_25_out,
       and_26_out, and_27_out, and_28_out, and_29_out, and_30_out, and_31_out;

  Decoder #(.select(5), .enable("false")) decoder_1 (.sel(Rw));  // open: out0, out1, out2, out3, out4, out5, out6, out7, out8, out9, out10, out11, out12, out13, out14, out15, out16, out17, out18, out19, out20, out21, out22, out23, out24, out25, out26, out27, out28, out29, out30, out31
  Register #(.width(32)) _0 ();  // open: D, en, Q, clk, clr
  Register #(.width(32)) _1 (.en(and_1_out));  // open: D, Q, clk, clr
  buf and_1 (and_1_out, W);  // AND_Gate
  Register #(.width(32)) _2 (.en(and_2_out));  // open: D, Q, clk, clr
  buf and_2 (and_2_out, W);  // AND_Gate
  Register #(.width(32)) _3 (.en(and_3_out));  // open: D, Q, clk, clr
  buf and_3 (and_3_out, W);  // AND_Gate
  Register #(.width(32)) _4 (.en(and_4_out));  // open: D, Q, clk, clr
  buf and_4 (and_4_out, W);  // AND_Gate
  Register #(.width(32)) _5 (.en(and_5_out));  // open: D, Q, clk, clr
  buf and_5 (and_5_out, W);  // AND_Gate
  Register #(.width(32)) _6 (.en(and_6_out));  // open: D, Q, clk, clr
  buf and_6 (and_6_out, W);  // AND_Gate
  Register #(.width(32)) _7 (.en(and_7_out));  // open: D, Q, clk, clr
  buf and_7 (and_7_out, W);  // AND_Gate
  Register #(.width(32)) _8 (.en(and_8_out));  // open: D, Q, clk, clr
  buf and_8 (and_8_out, W);  // AND_Gate
  Register #(.width(32)) _9 (.en(and_9_out));  // open: D, Q, clk, clr
  buf and_9 (and_9_out, W);  // AND_Gate
  Register #(.width(32)) _10 (.en(and_10_out));  // open: D, Q, clk, clr
  buf and_10 (and_10_out, W);  // AND_Gate
  Register #(.width(32)) _11 (.en(and_11_out));  // open: D, Q, clk, clr
  buf and_11 (and_11_out, W);  // AND_Gate
  Register #(.width(32)) _12 (.en(and_12_out));  // open: D, Q, clk, clr
  buf and_12 (and_12_out, W);  // AND_Gate
  Register #(.width(32)) _1_2 (.en(and_13_out));  // open: D, Q, clk, clr
  buf and_13 (and_13_out, W);  // AND_Gate
  Register #(.width(32)) _1_3 (.en(and_14_out));  // open: D, Q, clk, clr
  buf and_14 (and_14_out, W);  // AND_Gate
  Register #(.width(32)) _15 (.en(and_15_out));  // open: D, Q, clk, clr
  buf and_15 (and_15_out, W);  // AND_Gate
  Register #(.width(32)) _16 (.en(and_16_out));  // open: D, Q, clk, clr
  buf and_16 (and_16_out, W);  // AND_Gate
  Register #(.width(32)) _17 (.en(and_17_out));  // open: D, Q, clk, clr
  buf and_17 (and_17_out, W);  // AND_Gate
  Register #(.width(32)) _18 (.en(and_18_out));  // open: D, Q, clk, clr
  buf and_18 (and_18_out, W);  // AND_Gate
  Register #(.width(32)) _19 (.en(and_19_out));  // open: D, Q, clk, clr
  buf and_19 (and_19_out, W);  // AND_Gate
  Register #(.width(32)) _20 (.en(and_20_out));  // open: D, Q, clk, clr
  buf and_20 (and_20_out, W);  // AND_Gate
  Register #(.width(32)) _21 (.en(and_21_out));  // open: D, Q, clk, clr
  buf and_21 (and_21_out, W);  // AND_Gate
  Register #(.width(32)) _22 (.en(and_22_out));  // open: D, Q, clk, clr
  buf and_22 (and_22_out, W);  // AND_Gate
  Register #(.width(32)) _23 (.en(and_23_out));  // open: D, Q, clk, clr
  buf and_23 (and_23_out, W);  // AND_Gate
  Register #(.width(32)) _24 (.en(and_24_out));  // open: D, Q, clk, clr
  buf and_24 (and_24_out, W);  // AND_Gate
  Register #(.width(32)) _25 (.en(and_25_out));  // open: D, Q, clk, clr
  buf and_25 (and_25_out, W);  // AND_Gate
  Register #(.width(32)) _26 (.en(and_26_out));  // open: D, Q, clk, clr
  buf and_26 (and_26_out, W);  // AND_Gate
  Register #(.width(32)) _27 (.en(and_27_out));  // open: D, Q, clk, clr
  buf and_27 (and_27_out, W);  // AND_Gate
  Register #(.width(32)) _28 (.en(and_28_out));  // open: D, Q, clk, clr
  buf and_28 (and_28_out, W);  // AND_Gate
  Register #(.width(32)) _29 (.en(and_29_out));  // open: D, Q, clk, clr
  buf and_29 (and_29_out, W);  // AND_Gate
  Register #(.width(32)) _31 (.en(and_30_out));  // open: D, Q, clk, clr
  buf and_30 (and_30_out, W);  // AND_Gate
  Register #(.width(32)) _31_2 (.en(and_31_out));  // open: D, Q, clk, clr
  buf and_31 (and_31_out, W);  // AND_Gate
  Multiplexer #(.select(5), .width(32), .enable("false")) multiplexer_1 ();  // open: in0, in1, in2, in3, in4, in5, in6, in7, in8, in9, in10, in11, in12, in13, in14, in15, in16, in17, in18, in19, in20, in21, in22, in23, in24, in25, in26, in27, in28, in29, in30, in31, out, sel
  Multiplexer #(.select(5), .width(32), .enable("false")) multiplexer_2 ();  // open: in0, in1, in2, in3, in4, in5, in6, in7, in8, in9, in10, in11, in12, in13, in14, in15, in16, in17, in18, in19, in20, in21, in22, in23, in24, in25, in26, in27, in28, in29, in30, in31, out, sel
endmodule
